# Fritzing sketch IRHub (saved by Fritzing 0.9.3b)

parts:
  IR1 = TSOP312.., 314.. [package=THT]
  LED2 = LEDs [package=led10mm]  # not connected
  LED3 = LEDs [package=led10mm]  # not connected
  LED4 = LEDs [package=led10mm]  # not connected
  Q1 = NPN-Transistor [package="SOT-23 [SMD]"]
  LED1 = LEDs [package=led10mm]
  U1 = USB_AB [package=usb-ab-micro-smd]
  U2 = V_REG_LD1117VXX [package=78xxl]
  U3 = ESP8266 WiFi Module [part_number=ESP8266]

nets:
  N1: IR1.Data, U3.GPIO_0
  GND: Q1.2, U1.GND, U2.GND, U3.GND
  N2: Q1.0, U3.RXD
  N3: Q1.1, LED1.C
  N4: LED1.A, U2.OUT
  N5: U1.VBUS, U2.IN

custom parts:
  ESP8266 WiFi Module: Generic WiFi Module based on the ESP8266 with onboard PCB antenna and UART communications
