# Fritzing sketch SmartDoorbell (saved by Fritzing 0.9.3b)

parts:
  Mod1 = ESP32 - CAM
  PIR1 = PIR sensor
  X1 = USB Connectors [package=usb-microb]
  Grove1 = Grove OLED 128x96
  S1 = Pushbutton [package="[SMD]"]
  R1 = Resistor [tolerance=±5% resistance=220 package="0805 [SMD]"]

nets:
  N1: Mod1.5V, X1.VBUS
  GND: Mod1.GND, PIR1.GND, X1.GND, Grove1.GND, R1.Pin_1
  N2: Mod1.IO15, S1.Pin_1, S1.Pin_2, R1.Pin_0
  N3: Mod1.VOT, Grove1.SCL
  N4: Mod1.VOR, Grove1.SDA
  N5: Mod1.IO16, PIR1.SIG
  3V3: Mod1.3V3, PIR1.VDD, Grove1.VCC, S1.Pin_3, S1.Pin_4

custom parts:
  ESP32 - CAM: The ESP32-CAM has a very competitive small-size camera module that can operate independently as a minimum system with a footprint of only 27*40.5*4.5mm and a deep sleep current of up to 6mA.
