# Fritzing sketch WeatherStation (saved by Fritzing 0.9.3b)

parts:
  Part1 = Solar Cell
  Part2 = Solar Cell
  U1 = LIPO-2000mAh [package=lipo-2000]
  Part3 = PowerBoost 500 Charger
  U2 = ESP8266 WiFi Module [part_number=ESP8266]
  Part4 = Adafruit BMP180
  Part5 = BH1750  # not connected
  RHT1 = Humidity and Temperature Sensor RHT03
  YL-83_-_Control_Board1 = YL-83 Rain Sensor - Control Board
  YL-83_-_Detection_Board1 = YL-83 Rain Sensor - Detection Board

nets:
  N1: Part1.+, Part2.+, Part3.5.0V
  N2: Part1.-, Part3.GND
  VCC: U1.+, U2.VCC, Part4.+5V
  GND: U1.-, U2.GND, Part4.GND
  N3: U2.RXD, YL-83_-_Control_Board1.DO
  N4: U2.GPIO_0, Part4.SDA
  N5: U2.GPIO_2, Part4.SCL
  N6: U2.TXD, RHT1.Data-signal
  N7: YL-83_-_Control_Board1.POS, YL-83_-_Detection_Board1.POS
  N8: YL-83_-_Control_Board1.NEG, YL-83_-_Detection_Board1.NEG

custom parts:
  ESP8266 WiFi Module: Generic WiFi Module based on the ESP8266 with onboard PCB antenna and UART communications
  Adafruit BMP180: This precision sensor from Bosch is the best low-cost sensing solution for measuring barometric pressure and temperature. Because pressure changes with altitude you can also use it as an altimeter! The sensor is soldered onto a PCB with a 3.3V regulator, I2C level shifter and pull-up resistors on the I2C pins. The BMP180 is the next-generation of sensors from Bosch, and replaces the BMP085.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
  BH1750: Light Sensor
  YL-83 Rain Sensor - Control Board: The YL-83 is a rain sensor that has more resistance when dry and less resistance when wet. The module runs at 5V.
  YL-83 Rain Sensor - Detection Board: The YL-83 is a rain sensor that has more resistance when dry and less resistance when wet. The module runs at 5V.
